// Logisim project 1805098.circ as structural Verilog: 1 circuit, main circuit main
module main (
  input  P,
  input  Q,
  input  R,
  input  S,
  output Out
);

  wire n7404_1_p2, n7404_1_p4, n7404_1_p6, n7408_1_p3, n7408_1_p6;

  // _7404 7404_1: pin names not known; wires that end beside it: Q, n7404_1_p2, R, n7404_1_p4, S, n7404_1_p6, 1'b0, 1'b1
  // _7408 7408_1: pin names not known; wires that end beside it: P, n7404_1_p2, n7408_1_p3, n7408_1_p3, n7404_1_p4, n7408_1_p6, 1'b0, 1'b1
  // _7432 7432_1: pin names not known; wires that end beside it: n7408_1_p6, n7404_1_p6, Out, 1'b0, 1'b1
endmodule
