// Logisim project Nelson-10.8.circ as structural Verilog: 1 circuit, main circuit main
module main (
  input  x1,
  input  x2,
  output y1,
  output y2,
  output Z1,
  output Z2
);

  wire Clock_out, n7404_1_p2, n7404_1_p4, n7408_1_p3, n7408_1_p6, n7408_1_p9, n7408_1_p11, n7408_1_p12,
       n7408_2_p3, n7408_2_p6, n7408_2_p9, n7408_3_p3, n7408_4_p3, n7432_1_p2, n7432_1_p3, n7432_1_p6,
       n7432_2_p3, n7476_1_p2, n7476_2_p6;

  // _7404 7404_1: pin names not known; wires that end beside it: x1, n7404_1_p2, x2, n7404_1_p4
  // _7408 7408_1: pin names not known; wires that end beside it: n7404_1_p2, n7404_1_p4, n7408_1_p3, n7408_1_p3, y1, n7408_1_p6, x1, x2, n7408_1_p9, n7408_1_p9, n7408_1_p11, n7408_1_p12
  // _7408 7408_2: pin names not known; wires that end beside it: n7408_1_p3, y2, n7408_2_p3, n7408_1_p11, y2, n7408_2_p6, n7408_2_p6, n7404_1_p2, n7408_2_p9
  // _7432 7432_1: pin names not known; wires that end beside it: n7408_2_p3, n7432_1_p2, n7432_1_p3, n7432_1_p3, n7408_2_p9, n7432_1_p6
  // _7432 7432_2: pin names not known; wires that end beside it: n7408_1_p6, n7408_1_p12, n7432_2_p3
  Clock Clock (.out(Clock_out));
  // _7408 7408_3: pin names not known; wires that end beside it: x1, n7404_1_p4, n7408_3_p3
  // _7476 7476_1: pin names not known; wires that end beside it: Clock_out, n7476_1_p2, n7432_2_p3, n7432_2_p3, y1, n7408_1_p11
  Button Clear (.out(n7476_1_p2));
  // _7476 7476_2: pin names not known; wires that end beside it: Clock_out, n7476_1_p2, n7432_1_p6, n7432_1_p6, y2, n7476_2_p6
  // _7408 7408_4: pin names not known; wires that end beside it: n7408_1_p11, n7476_2_p6, n7408_4_p3, n7408_4_p3, n7408_3_p3, n7432_1_p2, y1, n7476_2_p6, Z1, y1, y2, Z2
endmodule
