// Logisim project Nelson-Exercise-10.9.circ as structural Verilog: 1 circuit, main circuit main
module main (
  input  x1,
  input  x2,
  output Z,
  output y
);

  wire n7408_1_p3, n7408_1_p4, n7408_1_p6, n7408_1_p7, n7408_1_p9, n7408_1_p10, n7408_1_p12, n7408_2_p2,
       n7408_2_p3, n7432_1_p3, n7432_1_p8;

  // _7408 7408_1: pin names not known; wires that end beside it: x1, x2, n7408_1_p3, n7408_1_p4, x2, n7408_1_p6, n7408_1_p7, y, n7408_1_p9, n7408_1_p10, n7408_1_p6, n7408_1_p12
  // _7432 7432_1: pin names not known; wires that end beside it: n7408_1_p9, n7408_1_p3, n7432_1_p3, x2, x1, n7408_1_p7, n7408_1_p12, n7432_1_p8, Z
  // _7408 7408_2: pin names not known; wires that end beside it: n7432_1_p8, n7408_2_p2, n7408_2_p3, n7408_2_p3, x1, y
  // _7404 7404_1: pin names not known; wires that end beside it: n7408_1_p4, x1, n7408_2_p2, x2, n7408_1_p10, y
  // _74116 74116_1: pin names not known; wires that end beside it: 1'b0, 1'b0, n7432_1_p3, y
endmodule
