// Logisim project 1805098_Asyncho.circ as structural Verilog: 1 circuit, main circuit main
module main (
  input  x1,
  input  x2,
  output Y,
  output out_4,
  output out_5,
  output out_6
);

  wire n7404_1_p2, n7404_1_p4;

  // _7404 7404_1: pin names not known; wires that end beside it: x2, n7404_1_p2, x1, n7404_1_p4
  // _74116 74116_1: pin names not known; wires that end beside it: out_5, out_4, out_6, Y
endmodule
