// Logisim project Group_2_Problem_4.circ as structural Verilog: 1 circuit, main circuit main
module main (
  input  A,
  input  B,
  input  C,
  input  D,
  output Output
);

  wire n7404_1_p2, n7404_1_p4, n7404_1_p6, n7404_1_p10, n7408_1_p3, n7408_1_p6, n7408_1_p11, n7408_2_p3,
       n7408_2_p6, n7408_2_p11, n7408_3_p3, n7408_3_p6, n7408_3_p11, n7408_4_p3, n7408_4_p6, n7432_1_p3,
       n7432_1_p5, n7432_1_p10;

  // _7404 7404_1: pin names not known; wires that end beside it: A, n7404_1_p2, B, n7404_1_p4, C, n7404_1_p6, 1'b0, 1'b1, D, n7404_1_p10
  // _7408 7408_1: pin names not known; wires that end beside it: n7404_1_p2, B, n7408_1_p3, n7408_1_p3, C, n7408_1_p6, 1'b0, 1'b1, n7408_1_p6, n7404_1_p10, n7408_1_p11
  // _7408 7408_2: pin names not known; wires that end beside it: A, n7404_1_p4, n7408_2_p3, n7408_2_p3, n7404_1_p6, n7408_2_p6, 1'b0, 1'b1, n7408_2_p6, D, n7408_2_p11
  // _7408 7408_3: pin names not known; wires that end beside it: A, B, n7408_3_p3, n7408_3_p3, n7404_1_p6, n7408_3_p6, 1'b0, 1'b1, n7408_3_p6, n7404_1_p10, n7408_3_p11
  // _7432 7432_1: pin names not known; wires that end beside it: n7408_2_p11, n7408_1_p11, n7432_1_p3, n7432_1_p3, n7432_1_p5, Output, 1'b0, 1'b1, n7408_3_p11, n7432_1_p10, n7432_1_p5
  // _7408 7408_4: pin names not known; wires that end beside it: A, B, n7408_4_p3, n7408_4_p3, C, n7408_4_p6, 1'b0, 1'b1, n7408_4_p6, D, n7432_1_p10, A, B, C, D, n7404_1_p2, n7404_1_p4, n7404_1_p6, n7404_1_p10
endmodule
