// Logisim project Group_B2_2_Problem_1.circ as structural Verilog: 1 circuit, main circuit main
module main (
  input  A,
  input  B,
  input  C,
  input  D,
  output F
);

  wire n7404_1_p5, n7404_1_p7, n7432_1_p1, n7432_1_p3;

  // _7404 7404_1: pin names not known; wires that end beside it: 1'b0, A, 1'b1, B, n7404_1_p5, D, n7404_1_p7, C
  // _7408 7408_1: pin names not known; wires that end beside it: n7404_1_p5, n7404_1_p7, 1'b1, D
  // _7432 7432_1: pin names not known; wires that end beside it: n7432_1_p1, 1'b0, n7432_1_p3, n7432_1_p1, F, 1'b0, B, n7432_1_p3, 1'b1
endmodule
