// Logisim project Group_B2_2_Problem_2.circ as structural Verilog: 1 circuit, main circuit main
module main (
  input  G2,
  input  G1,
  input  G0,
  output B2,
  output B1,
  output B0
);

  wire n7404_1_p2, n7404_1_p4, n7404_1_p6, n7404_1_p10, n7408_1_p3, n7408_1_p6, n7408_1_p11, n7408_1_p14;

  // _7404 7404_1: pin names not known; wires that end beside it: G2, n7404_1_p2, G1, n7404_1_p4, G0, n7404_1_p6, 1'b0, 1'b1, B1, n7404_1_p10
  // _7408 7408_1: pin names not known; wires that end beside it: G2, n7404_1_p4, n7408_1_p3, n7404_1_p2, G1, n7408_1_p6, 1'b0, 1'b1, n7404_1_p6, B1, n7408_1_p11, n7404_1_p10, G0, n7408_1_p14
  // _7432 7432_1: pin names not known; wires that end beside it: n7408_1_p6, n7408_1_p3, B1, n7408_1_p11, n7408_1_p14, B0, 1'b0, 1'b1

  assign B2 = G2;
endmodule
