// Logisim project Group_B2_2_Problem_3.circ as structural Verilog: 1 circuit, main circuit main
module main (
  input  A,
  input  B,
  input  C,
  output X,
  output Y
);

  wire n7404_1_p2, n7404_1_p4, n7404_1_p6, n7408_1_p3, n7408_1_p7, n7408_2_p2, n7408_2_p6, n7408_2_p10,
       n7408_2_p14, n7408_3_p2, n7408_3_p7, n7408_3_p11, n7408_3_p14, n7432_1_p3, n7432_1_p8, n7432_2_p2;

  // _7404 7404_1: pin names not known; wires that end beside it: A, n7404_1_p2, B, n7404_1_p4, C, n7404_1_p6, 1'b0, 1'b1
  // _7408 7408_1: pin names not known; wires that end beside it: A, B, n7408_1_p3, n7408_1_p3, n7404_1_p2, B, n7408_1_p7
  // _7408 7408_2: pin names not known; wires that end beside it: C, n7408_2_p2, 1'b0, A, n7404_1_p4, n7408_2_p6, n7408_2_p6, n7408_1_p7, n7404_1_p6, n7408_2_p10, 1'b1, n7404_1_p2, n7404_1_p4, n7408_2_p14
  // _7408 7408_3: pin names not known; wires that end beside it: n7404_1_p6, n7408_3_p2, 1'b0, 1'b0, n7408_2_p14, C, n7408_3_p7, 1'b1, B, C, n7408_3_p11, C, A, n7408_3_p14
  // _7432 7432_1: pin names not known; wires that end beside it: n7408_2_p2, n7408_3_p2, n7432_1_p3, n7432_1_p3, 1'b1, n7408_1_p3, n7408_3_p11, n7432_1_p8
  // _7432 7432_2: pin names not known; wires that end beside it: n7408_2_p10, n7432_2_p2, 1'b0, n7432_2_p2, n7408_3_p7, Y, 1'b0, n7432_1_p8, n7408_3_p14, X, 1'b1
endmodule
