// Logisim project Group_02_Problem_01.circ as structural Verilog: 1 circuit, main circuit main
module main (
  input  P1,
  input  P0,
  input  Q1,
  input  Q0,
  output G,
  output E,
  output L
);

  wire n7404_1_p2, n7404_1_p4, n7404_1_p5, n7404_1_p6, n7404_1_p10, n7404_1_p12, n7404_1_p13, n7404_1_p14,
       n7432_1_p1, n7432_1_p2, n7432_1_p4, n7432_1_p5, n7432_1_p9, n7432_1_p12;

  // _7404 7404_1: pin names not known; wires that end beside it: P0, n7404_1_p2, P1, n7404_1_p4, n7404_1_p5, n7404_1_p6, 1'b0, 1'b1, Q1, n7404_1_p10, Q0, n7404_1_p12, n7404_1_p13, n7404_1_p14
  // _7432 7432_1: pin names not known; wires that end beside it: n7432_1_p1, n7432_1_p2, n7404_1_p5, n7432_1_p4, n7432_1_p5, n7404_1_p13, 1'b0, 1'b1, n7432_1_p9, n7432_1_p5, G, n7432_1_p12, n7432_1_p4, L
  // _7408 7408_1: pin names not known; wires that end beside it: P1, n7404_1_p10, n7432_1_p5, n7404_1_p4, 1'b1
  // _7408 7408_2: pin names not known; wires that end beside it: Q1, n7432_1_p4, 1'b0, P0, n7404_1_p12, n7432_1_p2, n7404_1_p2, Q0, n7432_1_p1, 1'b0, n7432_1_p1, n7404_1_p14, n7432_1_p12, 1'b1, n7432_1_p2, n7404_1_p14, n7432_1_p9, n7404_1_p6, n7404_1_p14, E

  // Notes on the sheet:
  //   P1Q1'
  //   P1 XNOR Q1
  //   P0 XNOR Q0
  //   P1'Q1
  //   P0Q0'
  //   P0'Q0
endmodule
