// Logisim project Group_02_Problem_02.circ as structural Verilog: 1 circuit, main circuit main
module main (
  input  D,
  input  E,
  input  F,
  output R,
  output B
);

  wire n7404_1_p2, n7404_1_p4, n7404_1_p6, n7404_1_p9, n7404_1_p10, n7408_1_p3, n7408_1_p8, n7408_2_p2,
       n7408_2_p6, n7408_2_p9, n7408_2_p13, n7408_2_p16, n7432_1_p11;

  // _7404 7404_1: pin names not known; wires that end beside it: F, n7404_1_p2, E, n7404_1_p4, D, n7404_1_p6, 1'b0, 1'b1, n7404_1_p9, n7404_1_p10
  // _7408 7408_1: pin names not known; wires that end beside it: D, n7404_1_p4, n7408_1_p3, E, 1'b1, n7404_1_p10, F, n7408_1_p8
  // _7408 7408_2: pin names not known; wires that end beside it: n7404_1_p6, n7408_2_p2, 1'b0, n7404_1_p6, E, n7408_2_p6, n7404_1_p6, F, n7408_2_p9, 1'b0, n7404_1_p9, n7404_1_p2, n7408_2_p13, F, E, n7408_2_p16
  // _7432 7432_1: pin names not known; wires that end beside it: n7408_2_p2, n7408_1_p3, n7404_1_p9, n7408_1_p8, n7408_2_p13, R, 1'b0, 1'b1, n7408_2_p6, n7408_2_p9, n7432_1_p11, n7432_1_p11, n7408_2_p16, B
endmodule
