// Logisim project 1805098.circ as structural Verilog: 1 circuit, main circuit main
module main (
  input  D3,
  input  D2,
  input  D1,
  input  D0,
  output A1,
  output A0
);

  wire n7404_1_p3, n7404_1_p7, n7404_1_p9, n7408_1_p4;

  // _7404 7404_1: pin names not known; wires that end beside it: D2, D3, n7404_1_p3, 1'b0, 1'b1, D1, n7404_1_p7, D0, n7404_1_p9, D0
  // _7408 7408_1: pin names not known; wires that end beside it: n7404_1_p7, n7404_1_p9, n7404_1_p7, n7408_1_p4, A1, 1'b1
  // _7432 7432_1: pin names not known; wires that end beside it: 1'b0, n7404_1_p9, D3, n7408_1_p4, D1, D3, A0, 1'b0, 1'b1
endmodule
