// Logisim project 1805098.circ as structural Verilog: 1 circuit, main circuit main
module main (
  input  A,
  input  B,
  input  C,
  input  D,
  output out_5
);

  wire n74157_1_p5;

  // _74157 74157_1: pin names not known; wires that end beside it: D, D, 1'b1, 1'b0, n74157_1_p5, 1'b0
  // _74151 74151_1: pin names not known; wires that end beside it: D, D, 1'b0, 1'b0, out_5, 1'b0, 1'b0, 1'b0, 1'b1, n74157_1_p5, n74157_1_p5, C, B, A, 1'b0
endmodule
