// Logisim project 1805098_Online-4.circ as structural Verilog: 1 circuit, main circuit main
module main (
  output y2,
  output y1
);

  wire clock_1_out;

  Clock clock_1 (.out(clock_1_out));
  // _7476 T2: pin names not known; wires that end beside it: 1'b1, clock_1_out, 1'b0, 1'b1, y2, 1'b1
  // _7476 T1: pin names not known; wires that end beside it: 1'b1, clock_1_out, 1'b0, y2, y1, y2
endmodule
