// Logisim project 1805098_AdvanceCounter.circ as structural Verilog: 1 circuit, main circuit main
module main (
  output Y3,
  output Y2,
  output Y1
);

  wire clock_1_out, n7408_1_p4, T2_p4, T2_p6, T3_p4, T3_p6;

  Clock clock_1 (.out(clock_1_out));
  // _7476 T3: pin names not known; wires that end beside it: 1'b1, clock_1_out, 1'b0, T3_p4, Y3, T3_p6, T3_p4
  // _7404 7404_1: pin names not known; wires that end beside it: 1'b1, Y1, T3_p4
  // _7476 T2: pin names not known; wires that end beside it: 1'b1, clock_1_out, 1'b0, T2_p4, Y2, T2_p6, T2_p4
  // _7408 7408_1: pin names not known; wires that end beside it: 1'b1, T2_p6, T3_p6, n7408_1_p4
  // _7432 7432_1: pin names not known; wires that end beside it: n7408_1_p4, Y1, T2_p4, 1'b1
  // _7476 T1: pin names not known; wires that end beside it: 1'b1, clock_1_out, 1'b0, 1'b1, Y1, 1'b1
endmodule
