// Logisim project 1805098.circ as structural Verilog: 1 circuit, main circuit main
module main (
  input  x1,
  input  x2,
  output Z2,
  output Z1,
  output y1,
  output y0
);

  wire clock_1_out, n7404_1_p2, n7404_1_p4, n7404_1_p6, n7404_1_p8, n7408_1_p3, n7408_1_p6, n7408_1_p9,
       n7408_2_p3, n7408_2_p6, n7408_2_p9, n7408_3_p3, n7408_3_p6, n7408_3_p8, n7408_3_p9, n7408_4_p7,
       n7408_4_p9, n7408_4_p10, n7432_1_p3, n7432_3_p3, n7476_1_p2, n7476_1_p6;

  Clock clock_1 (.out(clock_1_out));
  // _7404 7404_1: pin names not known; wires that end beside it: x1, n7404_1_p2, x2, n7404_1_p4, y1, n7404_1_p6, y0, n7404_1_p8
  // _7408 7408_1: pin names not known; wires that end beside it: y1, x2, n7408_1_p3, x1, x2, n7408_1_p6, x1, y0, n7408_1_p9
  // _7408 7408_2: pin names not known; wires that end beside it: x1, n7404_1_p4, n7408_2_p3, y0, n7404_1_p2, n7408_2_p6, n7408_2_p6, x2, n7408_2_p9
  // _7408 7408_3: pin names not known; wires that end beside it: n7404_1_p2, n7404_1_p4, n7408_3_p3, x1, y1, n7408_3_p6, n7408_3_p6, n7408_3_p8, n7408_3_p9
  // _7408 7408_4: pin names not known; wires that end beside it: y1, n7404_1_p6, y0, n7404_1_p8, n7404_1_p2, x2, n7408_4_p7, n7408_4_p7, n7408_4_p9, n7408_4_p10
  // _7476 7476_1: pin names not known; wires that end beside it: clock_1_out, n7476_1_p2, clock_1_out, n7476_1_p2, y0, n7476_1_p6, y1, n7476_1_p6
  // _7432 7432_1: pin names not known; wires that end beside it: n7408_1_p3, n7408_1_p6, n7432_1_p3, n7432_1_p3, n7408_1_p9, n7476_1_p6, clock_1_out
  // _7432 7432_2: pin names not known; wires that end beside it: n7408_2_p3, n7408_2_p9, n7476_1_p2
  // _7432 7432_3: pin names not known; wires that end beside it: n7408_3_p3, n7408_3_p9, n7432_3_p3, x2, y0, n7408_3_p8
  // _7432 7432_4: pin names not known; wires that end beside it: y1, y0, n7408_4_p9
  // _7474 7474_1: pin names not known; wires that end beside it: n7408_4_p10, clock_1_out, Z2, n7432_3_p3, clock_1_out, Z1
endmodule
